// Logisim project CPU.circ as structural Verilog: 3 circuits, main circuit MAIN
module MAIN (
  input  in_1
);

  wire alu_1_carry_flag, alu_1_oflow_flag, alu_1_sign_flag, alu_1_zero_flag, clk_1_wave, STEP_out;
  wire [7:0] alu_1_result;

  Button STEP (.out(STEP_out));
  CLK clk_1 (.HALT(in_1), .STEP(STEP_out), .WAVE(clk_1_wave));
  ALU alu_1 (
    .OP_SUB(1'b0), .OP_AND(1'b0), .OP_OR(1'b0), .OP_XOR(1'b0), .OP_NOT(1'b0), .INPUT_A(8'h96),
    .INPUT_B(8'h96), .CARRY(1'b0), .OP_ADD(1'b1), .CARRY_FLAG(alu_1_carry_flag),
    .OFLOW_FLAG(alu_1_oflow_flag), .SIGN_FLAG(alu_1_sign_flag), .RESULT(alu_1_result),
    .ZERO_FLAG(alu_1_zero_flag));
endmodule

module ALU (
  input  [7:0] INPUT_A,
  input  [7:0] INPUT_B,
  input  CARRY,
  input  OP_ADD,
  input  OP_SUB,
  input  OP_AND,
  input  OP_OR,
  input  OP_XOR,
  input  OP_NOT,
  output [7:0] RESULT,
  output CARRY_FLAG,
  output OFLOW_FLAG,
  output SIGN_FLAG,
  output ZERO_FLAG
);

  wire and_1_out, and_2_out, and_3_out, and_4_out, and_5_out, and_6_out, and_7_out, and_8_out, and_9_out,
       and_10_out, and_11_out, and_12_out, and_13_out, and_14_out, and_15_out, and_16_out, and_18_out,
       and_20_out, and_21_out, and_22_out, nor_1_out, nor_2_out, nor_3_out, not_2_out, or_1_out, or_2_out,
       or_3_out, or_4_out, or_5_out, or_6_out, or_7_out, or_8_out, or_9_out, or_11_out, or_12_out, or_13_out,
       or_14_out, or_15_out, or_16_out, xor_2_out, xor_3_out, xor_4_out, xor_5_out, xor_6_out, xor_7_out,
       xor_8_out, xor_9_out;
  wire [7:0] and_17_out, not_1_out, or_10_out, xor_1_out, xor_10_out, xor_18_out;

  assign xor_1_out = INPUT_B ^ {8{OP_SUB}};  // XOR_Gate xor_1, 8 bits wide
  or or_1 (or_1_out, CARRY, OP_SUB);
  xor xor_2 (xor_2_out, INPUT_A[0], xor_1_out[0]);
  and and_1 (and_1_out, INPUT_A[0], xor_1_out[0]);
  xor xor_3 (xor_3_out, INPUT_A[1], xor_1_out[1]);
  and and_2 (and_2_out, INPUT_A[1], xor_1_out[1]);
  xor xor_4 (xor_4_out, INPUT_A[2], xor_1_out[2]);
  and and_3 (and_3_out, INPUT_A[2], xor_1_out[2]);
  xor xor_5 (xor_5_out, INPUT_A[3], xor_1_out[3]);
  and and_4 (and_4_out, INPUT_A[3], xor_1_out[3]);
  xor xor_6 (xor_6_out, INPUT_A[4], xor_1_out[4]);
  and and_5 (and_5_out, INPUT_A[4], xor_1_out[4]);
  xor xor_7 (xor_7_out, INPUT_A[5], xor_1_out[5]);
  and and_6 (and_6_out, INPUT_A[5], xor_1_out[5]);
  xor xor_8 (xor_8_out, INPUT_A[6], xor_1_out[6]);
  and and_7 (and_7_out, INPUT_A[6], xor_1_out[6]);
  xor xor_9 (xor_9_out, INPUT_A[7], xor_1_out[7]);
  and and_8 (and_8_out, INPUT_A[7], xor_1_out[7]);
  xor xor_10 (xor_10_out[0], xor_2_out, or_1_out);
  and and_9 (and_9_out, xor_2_out, or_1_out);
  or or_2 (or_2_out, and_9_out, and_1_out);
  xor xor_11 (xor_10_out[1], xor_3_out, or_2_out);
  and and_10 (and_10_out, xor_3_out, or_2_out);
  or or_3 (or_3_out, and_10_out, and_2_out);
  xor xor_12 (xor_10_out[2], xor_4_out, or_3_out);
  and and_11 (and_11_out, xor_4_out, or_3_out);
  or or_4 (or_4_out, and_11_out, and_3_out);
  xor xor_13 (xor_10_out[3], xor_5_out, or_4_out);
  and and_12 (and_12_out, xor_5_out, or_4_out);
  or or_5 (or_5_out, and_12_out, and_4_out);
  xor xor_14 (xor_10_out[4], xor_6_out, or_5_out);
  and and_13 (and_13_out, xor_6_out, or_5_out);
  or or_6 (or_6_out, and_13_out, and_5_out);
  xor xor_15 (xor_10_out[5], xor_7_out, or_6_out);
  and and_14 (and_14_out, xor_7_out, or_6_out);
  or or_7 (or_7_out, and_14_out, and_6_out);
  xor xor_16 (xor_10_out[6], xor_8_out, or_7_out);
  and and_15 (and_15_out, xor_8_out, or_7_out);
  or or_8 (or_8_out, and_15_out, and_7_out);
  xor xor_17 (xor_10_out[7], xor_9_out, or_8_out);
  and and_16 (and_16_out, xor_9_out, or_8_out);
  or or_9 (or_9_out, and_16_out, and_8_out);
  assign and_17_out = INPUT_A & xor_1_out;  // AND_Gate and_17, 8 bits wide
  assign or_10_out = INPUT_A | xor_1_out;  // OR_Gate or_10, 8 bits wide
  assign xor_18_out = INPUT_A ^ xor_1_out;  // XOR_Gate xor_18, 8 bits wide
  assign not_1_out = ~INPUT_A;  // NOT_Gate not_1, 8 bits wide
  assign RESULT = or_11_out ? xor_10_out : 8'bz;  // Controlled_Buffer controlled_buffer_1
  or or_11 (or_11_out, OP_ADD, OP_SUB);
  and and_18 (and_18_out, or_11_out, or_9_out);
  and and_19 (OFLOW_FLAG, or_11_out, or_12_out);
  nor nor_1 (nor_1_out, INPUT_A[7], xor_1_out[7]);
  and and_20 (and_20_out, INPUT_A[7], xor_1_out[7]);
  not not_2 (not_2_out, xor_10_out[7]);
  xor xor_19 (CARRY_FLAG, OP_SUB, and_18_out);
  or or_12 (or_12_out, and_21_out, and_22_out);
  and and_21 (and_21_out, nor_1_out, xor_10_out[7]);
  and and_22 (and_22_out, and_20_out, not_2_out);
  assign RESULT = OP_AND ? and_17_out : 8'bz;  // Controlled_Buffer controlled_buffer_2
  assign RESULT = OP_OR ? or_10_out : 8'bz;  // Controlled_Buffer controlled_buffer_3
  assign RESULT = OP_XOR ? xor_18_out : 8'bz;  // Controlled_Buffer controlled_buffer_4
  assign RESULT = OP_NOT ? not_1_out : 8'bz;  // Controlled_Buffer controlled_buffer_5
  or or_13 (or_13_out, RESULT[7], RESULT[6]);
  nor nor_2 (nor_2_out, or_13_out, or_14_out);
  or or_14 (or_14_out, RESULT[5], RESULT[4]);
  or or_15 (or_15_out, RESULT[3], RESULT[2]);
  nor nor_3 (nor_3_out, or_15_out, or_16_out);
  and and_23 (ZERO_FLAG, nor_2_out, nor_3_out);
  or or_16 (or_16_out, RESULT[1], RESULT[0]);

  assign SIGN_FLAG = RESULT[7];
endmodule

module CLK (
  input  HALT,
  input  STEP,
  output WAVE
);

  wire and_1_out, clock_1_out, not_1_out, or_1_out;

  Clock clock_1 (.out(clock_1_out));
  not not_1 (not_1_out, HALT);
  or or_1 (or_1_out, not_1_out, STEP);
  and and_1 (and_1_out, clock_1_out, or_1_out);
  or or_2 (WAVE, and_1_out, STEP);
endmodule
